# Fritzing sketch arduino mini wireless node (saved by Fritzing 0.9.1b)
circuit board: 8.46667cm x 5.64444cm
breadboards: 1

parts:
  Part1 = Arduino Pro Mini v13
  DS1 = DS18B20 1-Wire Temperature Sensor [part_number=DS18B20]
  R1 = Resistor [tolerance=±1% resistance=4.7k package=THT]
  R2 = Resistor [tolerance=±5% resistance=220 package=THT]
  R3 = Resistor [tolerance=±1% resistance=220 package=THT]
  D4 = Rectifier Diode [part_number=1N4001 package="300 mil [THT]"]
  D5 = Rectifier Diode [part_number=1N4001 package="300 mil [THT]"]
  D6 = Rectifier Diode [part_number=1N4001 package="300 mil [THT]"]
  NRF24L1 = NRF24L01
  VCC1 = 4 x AAA Battery Mount

nets:
  N1: Part1.RAW, NRF24L1.GND, VCC1.+
  GND: Part1.GND, Part1.D9_PWM, Part1.D5_PWM, DS1.GND, R1.Pin_1, R2.Pin_1, R3.Pin_0, VCC1.-
  VCC: Part1.VCC, DS1.VDD, D4.anode
  N2: Part1.A0, R2.Pin_0, R3.Pin_1
  N3: Part1.D13/SCK, NRF24L1.SCK
  N4: Part1.D12/MISO, NRF24L1.MOSI
  N5: Part1.D11_PWM/MOSI, NRF24L1.MISO
  N6: Part1.D8, NRF24L1.CSN
  N7: Part1.D7, NRF24L1.CE
  N8: Part1.D4, DS1.DQ, R1.Pin_0
  N9: D4.cathode, D5.anode
  N10: D5.cathode, D6.anode
  N11: D6.cathode, NRF24L1.VCC

custom parts:
  NRF24L01: NRF24L01 module
