# Fritzing sketch arduino uno wireless node master (saved by Fritzing 0.9.1b)
breadboards: 1

parts:
  Part1 = Arduino Uno (Rev3) - ICSP
  NRF24L1 = NRF24L01

nets:
  N1: Part1.D11_PWM/MOSI, NRF24L1.MISO
  N2: Part1.D12/MISO, NRF24L1.MOSI
  N3: Part1.D13/SCK, NRF24L1.SCK
  N4: Part1.D2, NRF24L1.IRQ
  N5: Part1.D6_PWM, NRF24L1.CE
  N6: Part1.D7, NRF24L1.CSN
  3V3: Part1.3V3, NRF24L1.VCC
  GND: Part1.GND, NRF24L1.GND

custom parts:
  NRF24L01: NRF24L01 module
