# Fritzing sketch arduino uno wireless weather node master (saved by Fritzing 0.9.1b)
breadboards: 1

parts:
  NRF24L1 = NRF24L01
  Part1 = Arduino Uno (Rev3) - ICSP
  U1 = RF-LINK_RX [package=rf-link_rx]
  C1 = Ceramic Capacitor [capacitance="100 nF" package="1206 [SMD, multilayer]"]
  ANT1 = Antenna

nets:
  VCC: NRF24L1.VCC, Part1.3V3
  N1: NRF24L1.CSN, Part1.D7
  N2: NRF24L1.MOSI, Part1.D12/MISO
  N3: NRF24L1.IRQ, Part1.D2
  GND: NRF24L1.GND, Part1.GND, U1.GND, C1.1
  N4: NRF24L1.CE, Part1.D6_PWM
  N5: NRF24L1.SCK, Part1.D13/SCK
  N6: NRF24L1.MISO, Part1.D11_PWM/MOSI
  N7: Part1.D8, U1.DATA
  5V: Part1.5V, U1.+5V, C1.0
  N8: U1.ANT, ANT1.antenna_lead

custom parts:
  NRF24L01: NRF24L01 module
